// Logisim project 7_segment_display.circ as structural Verilog: 1 circuit, main circuit main
module main (
  input  [2:0] in_1
);

  wire _0_out, _1_out, _2_out, _3_out, _4_out, _5_out, _6_out, _7_out, not_1_out, not_2_out, not_3_out,
       T_out, U_out, V_out, W_out, X_out, Y_out, Z_out;

  not not_1 (not_1_out, in_1[0]);
  not not_2 (not_2_out, in_1[1]);
  not not_3 (not_3_out, in_1[2]);
  and _0 (_0_out, not_3_out, not_2_out, not_1_out);
  and _1 (_1_out, not_3_out, not_2_out, in_1[0]);
  and _2 (_2_out, not_3_out, in_1[1], not_1_out);
  or Z (Z_out, _6_out, _5_out, _4_out, _3_out, _2_out);
  or Y (Y_out, _6_out, _5_out, _4_out, _0_out);
  or X (X_out, _6_out, _2_out, _0_out);
  or W (W_out, _6_out, _5_out, _3_out, _2_out, _0_out);
  or V (V_out, _7_out, _6_out, _5_out, _4_out, _3_out, _1_out, _0_out);
  or U (U_out, _7_out, _4_out, _3_out, _2_out, _1_out, _0_out);
  or T (T_out, _7_out, _6_out, _5_out, _3_out, _2_out, _0_out);
  and _4 (_4_out, in_1[2], not_2_out, not_1_out);
  and _3 (_3_out, not_3_out, in_1[1], in_1[0]);
  _7_Segment_Display u_7_segment_display_1 (
    .g(Z_out), .f(Y_out), .a(T_out), .b(U_out), .e(X_out), .d(W_out), .c(V_out));  // open: dp
  and _5 (_5_out, in_1[2], not_2_out, in_1[0]);
  and _6 (_6_out, in_1[2], in_1[1], not_1_out);
  and _7 (_7_out, in_1[2], in_1[1], in_1[0]);
endmodule
