// Logisim project nand_gates.circ as structural Verilog: 1 circuit, main circuit main
module main (
  input  Opdracht_3,
  input  A,
  input  in_3,
  input  B,
  input  C,
  input  in_6,
  input  in_7,
  input  in_8,
  input  in_9,
  input  in_10,
  output out_11,
  output X,
  output Y,
  output out_14,
  output out_15,
  output out_16
);

  wire and_1_out, and_2_out, nand_1_out, nand_2_out, nand_4_out, or_1_out;

  and and_1 (and_1_out, Opdracht_3, in_3);
  not not_1 (out_11, and_1_out);
  not nand_1 (nand_1_out, in_6);  // NAND_Gate
  not nand_2 (nand_2_out, in_7);  // NAND_Gate
  not nand_3 (out_15, in_8);  // NAND_Gate
  nand nand_4 (nand_4_out, in_9, in_10);
  nand nand_5 (out_14, nand_1_out, nand_2_out);
  not nand_6 (out_16, nand_4_out);  // NAND_Gate
  or or_1 (or_1_out, A, B);
  and and_2 (and_2_out, B, C);
  nor nor_1 (X, B, and_2_out);
  nand nand_7 (Y, or_1_out, C);

  // Notes on the sheet:
  //   Opdracht 4
endmodule
