// Logisim project truthtable_implementation.circ as structural Verilog: 1 circuit, main circuit main
module main (
  input  A,
  input  B,
  input  C,
  output X,
  output Y
);

  wire and_1_out, not_1_out, not_2_out, not_3_out, or_1_out;

  not not_1 (not_1_out, A);
  not not_2 (not_2_out, B);
  not not_3 (not_3_out, C);
  or or_1 (or_1_out, not_1_out, not_3_out);
  and and_1 (and_1_out, not_1_out, not_3_out);
  and and_2 (X, or_1_out, not_2_out);
  or or_2 (Y, X, and_1_out);

  // Notes on the sheet:
  //   Opdracht 4
endmodule
