// Logisim project 12-bit_adder.circ as structural Verilog: 2 circuits, main circuit 1-bit adder
module _1_bit_adder (
  input  Ci,
  input  A,
  input  B,
  output R,
  output Co
);

  wire and_1_out, and_2_out, xor_1_out;

  xor xor_1 (xor_1_out, A, B);
  and and_1 (and_1_out, B, A);
  xor xor_2 (R, Ci, xor_1_out);
  and and_2 (and_2_out, xor_1_out, Ci);
  or or_1 (Co, and_2_out, and_1_out);
endmodule

module _12_bit_adder (
  input  [11:0] A,
  input  in_2,
  input  [11:0] B,
  output [11:0] R,
  output Overflow
);

  wire _0_co, _1_co, _2_co, _3_co, n1_bit_adder_1_co, n1_bit_adder_2_co, n1_bit_adder_3_co,
       n1_bit_adder_4_co, n1_bit_adder_5_co, n1_bit_adder_6_co, n1_bit_adder_7_co, n1_bit_adder_8_co,
       xnor_1_out, xor_1_out;

  _1_bit_adder _0 (.A(A[0]), .B(B[0]), .Ci(in_2), .Co(_0_co), .R(R[0]));
  _1_bit_adder _1 (.A(A[1]), .B(B[1]), .Ci(_0_co), .Co(_1_co), .R(R[1]));
  _1_bit_adder _2 (.A(A[2]), .B(B[2]), .Ci(_1_co), .Co(_2_co), .R(R[2]));
  _1_bit_adder _3 (.A(A[3]), .B(B[3]), .Ci(_2_co), .Co(_3_co), .R(R[3]));
  _1_bit_adder u_1_bit_adder_1 (.A(A[4]), .B(B[4]), .Ci(_3_co), .Co(n1_bit_adder_1_co), .R(R[4]));
  _1_bit_adder u_1_bit_adder_2 (.A(A[5]), .B(B[5]), .Ci(n1_bit_adder_1_co), .Co(n1_bit_adder_2_co), .R(R[5]));
  _1_bit_adder u_1_bit_adder_3 (.A(A[6]), .B(B[6]), .Ci(n1_bit_adder_2_co), .Co(n1_bit_adder_3_co), .R(R[6]));
  _1_bit_adder u_1_bit_adder_4 (.A(A[7]), .B(B[7]), .Ci(n1_bit_adder_3_co), .Co(n1_bit_adder_4_co), .R(R[7]));
  _1_bit_adder u_1_bit_adder_5 (.A(A[8]), .B(B[8]), .Ci(n1_bit_adder_4_co), .Co(n1_bit_adder_5_co), .R(R[8]));
  _1_bit_adder u_1_bit_adder_6 (.A(A[9]), .B(B[9]), .Ci(n1_bit_adder_5_co), .Co(n1_bit_adder_6_co), .R(R[9]));
  _1_bit_adder u_1_bit_adder_7 (.A(A[10]), .B(B[10]), .Ci(n1_bit_adder_6_co), .Co(n1_bit_adder_7_co), .R(R[10]));
  _1_bit_adder u_1_bit_adder_8 (.A(A[11]), .B(B[11]), .Ci(n1_bit_adder_7_co), .Co(n1_bit_adder_8_co), .R(R[11]));
  xor xor_1 (xor_1_out, R[11], n1_bit_adder_8_co);
  xnor xnor_1 (xnor_1_out, A[11], B[11]);
  and and_1 (Overflow, xor_1_out, xnor_1_out);
endmodule
