// Logisim project 12-bit ALU.circ as structural Verilog: 15 circuits, main circuit 12-bit ALU
module _12_bit_ALU (
  input  [3:0] Selector,
  input  [11:0] Operand_A,
  input  [11:0] Operand_B,
  output [11:0] Result,
  output Overflow
);

  wire add_1_overflow, inv_1_overflow, sla_1_overflow, sub_1_overflow;
  wire [11:0] ADD, AND, EQ, GT, INV, LT, NEQ, NOT, OR, SLA, SLL, SRA, SRL, SUB;

  AND and_1 (.Operand_A(Operand_A), .Operand_B(Operand_B), .Resultaat(AND));
  OR or_1 (.Operand_A(Operand_A), .Operand_B(Operand_B), .out_3(OR));
  NOT not_1 (.Operand_A(Operand_A), .Resultaat(NOT));
  SLL sll_1 (.Operand_A(Operand_A), .Resultaat(SLL));
  SLA sla_1 (.Operand_A(Operand_A), .Resultaat(SLA), .Overflow(sla_1_overflow));
  SRL srl_1 (.Operand_A(Operand_A), .Resultaat(SRL));
  SRA sra_1 (.Operand_A(Operand_A), .Resultaat(SRA));
  ADD add_1 (.Operand_A(Operand_A), .Operand_B(Operand_B), .Resultaat(ADD), .Overflow(add_1_overflow), .Ci(1'b0));
  SUB sub_1 (.Operand_A(Operand_A), .Operand_B(Operand_B), .Overflow(sub_1_overflow), .Resultaat(SUB));
  LT lt_1 (.Resultaat(LT), .Operand_A(Operand_A), .Operand_B(Operand_B));
  GT gt_1 (.Operand_A(Operand_A), .Operand_B(Operand_B), .Resultaat(GT));
  NEQ neq_1 (.Operand_A(Operand_A), .Operand_B(Operand_B), .Resultaat(NEQ));
  EQ eq_1 (.Operand_A(Operand_A), .Operand_B(Operand_B), .Resultaat(EQ));
  INV inv_1 (.Operand_A(Operand_A), .Resultaat(INV), .Overflow(inv_1_overflow));
  Multiplexer #(.select(4), .width(12)) multiplexer_1 (
    .in0(ADD), .in1(SUB), .in2(AND), .in3(OR), .in4(LT), .in5(GT), .in6(EQ), .in7(NEQ), .in8(NOT), .in9(INV),
    .in10(SLL), .in11(SRL), .in12(SLA), .in13(SRA), .in14({12{1'b0}}), .in15(Operand_A), .out(Result),
    .sel(Selector));  // open: en
  Multiplexer #(.select(4)) multiplexer_2 (
    .in0(add_1_overflow), .in1(sub_1_overflow), .in2(1'b0), .in3(1'b0), .in4(1'b0), .in5(1'b0), .in6(1'b0),
    .in7(1'b0), .in8(1'b0), .in9(inv_1_overflow), .in10(1'b0), .in11(1'b0), .in12(sla_1_overflow),
    .in13(1'b0), .in14(1'b0), .in15(1'b0), .out(Overflow), .sel(Selector));  // open: en

  // Other names for the same wires on the sheet: A[11:0] = Operand_A
endmodule

module AND (
  input  [11:0] Operand_A,
  input  [11:0] Operand_B,
  output [11:0] Resultaat
);

  assign Resultaat = Operand_A & Operand_B;  // AND_Gate and_1, 12 bits wide
endmodule

module OR (
  input  [11:0] Operand_A,
  input  [11:0] Operand_B,
  output [11:0] out_3
);

  assign out_3 = Operand_A | Operand_B;  // OR_Gate or_1, 12 bits wide
endmodule

module NOT (
  input  [11:0] Operand_A,
  output [11:0] Resultaat
);

  assign Resultaat = ~Operand_A;  // NOT_Gate not_1, 12 bits wide
endmodule

module SLL (
  input  [11:0] Operand_A,
  output [11:0] Resultaat
);


  assign Resultaat = {Operand_A[10:0], 1'b0};
endmodule

module SLA (
  input  [11:0] Operand_A,
  output [11:0] Resultaat,
  output Overflow
);

  xor xor_1 (Overflow, Operand_A[11], Operand_A[10]);

  assign Resultaat = {Operand_A[10:0], 1'b0};
endmodule

module SRL (
  input  [11:0] Operand_A,
  output [11:0] Resultaat
);


  assign Resultaat = {1'b0, Operand_A[11:1]};
endmodule

module SRA (
  input  [11:0] Operand_A,
  output [11:0] Resultaat
);


  assign Resultaat = {{2{Operand_A[11]}}, Operand_A[10:1]};
endmodule

module ADD (
  input  Ci,
  input  [11:0] Operand_A,
  input  [11:0] Operand_B,
  output [11:0] Resultaat,
  output Overflow
);

  // _12_bit_Carry_Lookahead 12_bit_carry_lookahead_1: pin names not known; wires that end beside it: Ci, Operand_A, Operand_B, Resultaat, Overflow
endmodule

module SUB (
  input  [11:0] Operand_A,
  input  [11:0] Operand_B,
  output [11:0] Resultaat,
  output Overflow
);

  wire [11:0] not_1_out;

  assign not_1_out = ~Operand_B;  // NOT_Gate not_1, 12 bits wide
  ADD add_1 (.Operand_A(Operand_A), .Operand_B(not_1_out), .Resultaat(Resultaat), .Overflow(Overflow), .Ci(1'b1));
endmodule

module LT (
  input  [11:0] Operand_A,
  input  [11:0] Operand_B,
  output [11:0] Resultaat
);

  wire sub_1_overflow;
  wire [11:0] sub_1_resultaat;

  SUB sub_1 (.Operand_A(Operand_A), .Operand_B(Operand_B), .Overflow(sub_1_overflow), .Resultaat(sub_1_resultaat));
  xor xor_1 (Resultaat[0], sub_1_resultaat[11], sub_1_overflow);

  assign Resultaat[11:1] = {11{1'b0}};
endmodule

module NEQ (
  input  [11:0] Operand_A,
  input  [11:0] Operand_B,
  output [11:0] Resultaat
);

  wire xor_1_out, xor_2_out, xor_3_out, xor_4_out, xor_5_out, xor_6_out, xor_7_out, xor_8_out, xor_9_out,
       xor_10_out, xor_11_out, xor_12_out;

  xor xor_1 (xor_1_out, Operand_A[0], Operand_B[0]);
  xor xor_2 (xor_2_out, Operand_A[1], Operand_B[1]);
  xor xor_3 (xor_3_out, Operand_A[2], Operand_B[2]);
  xor xor_4 (xor_4_out, Operand_A[3], Operand_B[3]);
  xor xor_5 (xor_5_out, Operand_A[4], Operand_B[4]);
  xor xor_6 (xor_6_out, Operand_A[5], Operand_B[5]);
  xor xor_7 (xor_7_out, Operand_A[6], Operand_B[6]);
  xor xor_8 (xor_8_out, Operand_A[7], Operand_B[7]);
  xor xor_9 (xor_9_out, Operand_A[8], Operand_B[8]);
  xor xor_10 (xor_10_out, Operand_A[9], Operand_B[9]);
  xor xor_11 (xor_11_out, Operand_A[10], Operand_B[10]);
  xor xor_12 (xor_12_out, Operand_A[11], Operand_B[11]);
  or or_1 (Resultaat[0], xor_1_out, xor_2_out, xor_3_out, xor_4_out, xor_5_out, xor_6_out, xor_7_out, xor_8_out, xor_9_out, xor_10_out, xor_11_out, xor_12_out);

  assign Resultaat[11:1] = {11{1'b0}};
endmodule

module EQ (
  input  [11:0] Operand_A,
  input  [11:0] Operand_B,
  output [11:0] Resultaat
);

  wire or_1_out, xor_1_out, xor_2_out, xor_3_out, xor_4_out, xor_5_out, xor_6_out, xor_7_out, xor_8_out,
       xor_9_out, xor_10_out, xor_11_out, xor_12_out;

  xor xor_1 (xor_1_out, Operand_A[0], Operand_B[0]);
  xor xor_2 (xor_2_out, Operand_A[1], Operand_B[1]);
  xor xor_3 (xor_3_out, Operand_A[2], Operand_B[2]);
  xor xor_4 (xor_4_out, Operand_A[3], Operand_B[3]);
  xor xor_5 (xor_5_out, Operand_A[4], Operand_B[4]);
  xor xor_6 (xor_6_out, Operand_A[5], Operand_B[5]);
  xor xor_7 (xor_7_out, Operand_A[6], Operand_B[6]);
  xor xor_8 (xor_8_out, Operand_A[7], Operand_B[7]);
  xor xor_9 (xor_9_out, Operand_A[8], Operand_B[8]);
  xor xor_10 (xor_10_out, Operand_A[9], Operand_B[9]);
  xor xor_11 (xor_11_out, Operand_A[10], Operand_B[10]);
  xor xor_12 (xor_12_out, Operand_A[11], Operand_B[11]);
  not not_1 (Resultaat[0], or_1_out);
  or or_1 (or_1_out, xor_1_out, xor_2_out, xor_3_out, xor_4_out, xor_5_out, xor_6_out, xor_7_out, xor_8_out, xor_9_out, xor_10_out, xor_11_out, xor_12_out);

  assign Resultaat[11:1] = {11{1'b0}};
endmodule

module GT (
  input  [11:0] Operand_A,
  input  [11:0] Operand_B,
  output [11:0] Resultaat
);

  wire not_1_out, not_2_out, sub_1_overflow, xor_1_out;
  wire [11:0] eq_1_resultaat, sub_1_resultaat;

  SUB sub_1 (.Operand_A(Operand_A), .Operand_B(Operand_B), .Overflow(sub_1_overflow), .Resultaat(sub_1_resultaat));
  EQ eq_1 (.Operand_A(Operand_A), .Operand_B(Operand_B), .Resultaat(eq_1_resultaat));
  not not_1 (not_1_out, eq_1_resultaat[0]);
  not not_2 (not_2_out, sub_1_resultaat[11]);
  xor xor_1 (xor_1_out, not_2_out, sub_1_overflow);
  and and_1 (Resultaat[0], not_1_out, xor_1_out);

  assign Resultaat[11:1] = {11{1'b0}};
endmodule

module INV (
  input  [11:0] Operand_A,
  output [11:0] Resultaat,
  output Overflow
);

  wire [11:0] not_1_out;

  assign not_1_out = ~Operand_A;  // NOT_Gate not_1, 12 bits wide
  ADD add_1 (.Operand_A(not_1_out), .Operand_B({12{1'b0}}), .Resultaat(Resultaat), .Overflow(Overflow), .Ci(1'b1));
endmodule
