// Logisim project 12-bit_lookahead_adder.circ as structural Verilog: 3 circuits, main circuit 4-bit Carry Lookahead
module _4_bit_Carry_Lookahead (
  input  [3:0] A,
  input  [3:0] B,
  input  c0,
  output [3:0] S,
  output G0,
  output P0
);

  wire and_1_out, and_2_out, and_3_out, and_4_out, and_5_out, and_6_out, and_8_out, and_9_out, and_10_out,
       c1_out, c2_out, c3_out, g0_out, g1_out, g2_out, g3_out, p0_out, p1_out, p2_out, p3_out, xor_2_out,
       xor_4_out, xor_6_out, xor_8_out;

  and g3 (g3_out, B[3], A[3]);
  or p3 (p3_out, B[3], A[3]);
  and g2 (g2_out, B[2], A[2]);
  or p2 (p2_out, B[2], A[2]);
  and and_1 (and_1_out, p0_out, c0);
  and and_2 (and_2_out, g1_out, p2_out);
  and and_3 (and_3_out, g0_out, p1_out);
  and and_4 (and_4_out, g0_out, p1_out, p2_out, p3_out);
  and and_5 (and_5_out, g1_out, p2_out, p3_out);
  and and_6 (and_6_out, g2_out, p3_out);
  and and_7 (P0, p0_out, p1_out, p2_out, p3_out);
  and g1 (g1_out, B[1], A[1]);
  and and_8 (and_8_out, and_1_out, p1_out);
  and and_9 (and_9_out, and_8_out, p2_out);
  and and_10 (and_10_out, and_3_out, p2_out);
  or or_1 (G0, and_4_out, and_5_out, and_6_out, g3_out);
  and u_g0 (g0_out, B[0], A[0]);
  or p1 (p1_out, B[1], A[1]);
  or u_p0 (p0_out, B[0], A[0]);
  or c1 (c1_out, g0_out, and_1_out);
  or c2 (c2_out, and_8_out, g1_out, and_3_out);
  or c3 (c3_out, and_9_out, g2_out, and_2_out, and_10_out);
  xor xor_1 (S[0], c0, xor_2_out);
  xor xor_2 (xor_2_out, A[0], B[0]);
  xor xor_3 (S[1], c1_out, xor_4_out);
  xor xor_4 (xor_4_out, A[1], B[1]);
  xor xor_5 (S[2], c2_out, xor_6_out);
  xor xor_6 (xor_6_out, A[2], B[2]);
  xor xor_7 (S[3], c3_out, xor_8_out);
  xor xor_8 (xor_8_out, A[3], B[3]);
endmodule

module Carry_Lookahead_Unit (
  input  G2,
  input  P2,
  input  G1,
  input  P1,
  input  G0,
  input  P0,
  input  C0,
  output C3,
  output C2,
  output C1
);

  wire and_1_out, and_2_out, and_3_out, and_4_out, and_5_out, and_6_out;

  and and_1 (and_1_out, P1, G0);
  and and_2 (and_2_out, P0, C0);
  and and_3 (and_3_out, P1, P0, C0);
  and and_4 (and_4_out, P2, G1);
  and and_5 (and_5_out, P2, and_3_out);
  and and_6 (and_6_out, P2, and_1_out);
  or or_1 (C3, G2, and_4_out, and_5_out, and_6_out);
  or or_2 (C2, G1, and_3_out, and_1_out);
  or or_3 (C1, G0, and_2_out);
endmodule

module _12_bit_Carry_Lookahead (
  input  Ci,
  input  [11:0] A,
  input  [11:0] B,
  output [11:0] S,
  output Overflow__Co
);

  wire carry_lookahead_unit_1_c1, carry_lookahead_unit_1_c2, carry_lookahead_unit_1_c3,
       n4_bit_carry_lookahead_1_g0, n4_bit_carry_lookahead_1_p0, n4_bit_carry_lookahead_2_g0,
       n4_bit_carry_lookahead_2_p0, n4_bit_carry_lookahead_3_g0, n4_bit_carry_lookahead_3_p0, xnor_1_out,
       xor_1_out;

  _4_bit_Carry_Lookahead u_4_bit_carry_lookahead_1 (
    .A(A[11:8]), .B(B[11:8]), .c0(carry_lookahead_unit_1_c2), .S(S[11:8]), .G0(n4_bit_carry_lookahead_1_g0),
    .P0(n4_bit_carry_lookahead_1_p0));
  Carry_Lookahead_Unit carry_lookahead_unit_1 (
    .C3(carry_lookahead_unit_1_c3), .C2(carry_lookahead_unit_1_c2), .C1(carry_lookahead_unit_1_c1),
    .G2(n4_bit_carry_lookahead_1_g0), .P2(n4_bit_carry_lookahead_1_p0), .G1(n4_bit_carry_lookahead_2_g0),
    .P1(n4_bit_carry_lookahead_2_p0), .G0(n4_bit_carry_lookahead_3_g0), .P0(n4_bit_carry_lookahead_3_p0),
    .C0(Ci));
  _4_bit_Carry_Lookahead u_4_bit_carry_lookahead_2 (
    .A(A[7:4]), .B(B[7:4]), .c0(carry_lookahead_unit_1_c1), .S(S[7:4]), .G0(n4_bit_carry_lookahead_2_g0),
    .P0(n4_bit_carry_lookahead_2_p0));
  _4_bit_Carry_Lookahead u_4_bit_carry_lookahead_3 (
    .A(A[3:0]), .B(B[3:0]), .c0(Ci), .S(S[3:0]), .G0(n4_bit_carry_lookahead_3_g0),
    .P0(n4_bit_carry_lookahead_3_p0));
  xor xor_1 (xor_1_out, S[11], carry_lookahead_unit_1_c3);
  xnor xnor_1 (xnor_1_out, B[11], A[11]);
  and and_1 (Overflow__Co, xor_1_out, xnor_1_out);
endmodule
