// Logisim project Register.circ as structural Verilog: 5 circuits, main circuit register
// reg
module register (
  input  [11:0] D,
  input  Clock,
  input  Write,
  input  Reset,
  output [11:0] Q
);

  wire and_1_out;

  and and_1 (and_1_out, Clock, Write);
  D_Flip_Flop #(.trigger("falling")) d_ff_1 (
    .clk(and_1_out), .D(D[11]), .Q(Q[11]), .reset(Reset));  // open: Qn, preset, en
  D_Flip_Flop #(.trigger("falling")) d_ff_2 (
    .clk(and_1_out), .D(D[9]), .Q(Q[9]), .reset(Reset));  // open: Qn, preset, en
  D_Flip_Flop #(.trigger("falling")) d_ff_3 (
    .clk(and_1_out), .D(D[10]), .Q(Q[10]), .reset(Reset));  // open: Qn, preset, en
  D_Flip_Flop #(.trigger("falling")) d_ff_4 (
    .clk(and_1_out), .D(D[7]), .Q(Q[7]), .reset(Reset));  // open: Qn, preset, en
  D_Flip_Flop #(.trigger("falling")) d_ff_5 (
    .clk(and_1_out), .D(D[8]), .Q(Q[8]), .reset(Reset));  // open: Qn, preset, en
  D_Flip_Flop #(.trigger("falling")) d_ff_6 (
    .clk(and_1_out), .D(D[5]), .Q(Q[5]), .reset(Reset));  // open: Qn, preset, en
  D_Flip_Flop #(.trigger("falling")) d_ff_7 (
    .clk(and_1_out), .D(D[6]), .Q(Q[6]), .reset(Reset));  // open: Qn, preset, en
  D_Flip_Flop #(.trigger("falling")) d_ff_8 (
    .clk(and_1_out), .D(D[3]), .Q(Q[3]), .reset(Reset));  // open: Qn, preset, en
  D_Flip_Flop #(.trigger("falling")) d_ff_9 (
    .clk(and_1_out), .D(D[4]), .Q(Q[4]), .reset(Reset));  // open: Qn, preset, en
  D_Flip_Flop #(.trigger("falling")) d_ff_10 (
    .clk(and_1_out), .D(D[1]), .Q(Q[1]), .reset(Reset));  // open: Qn, preset, en
  D_Flip_Flop #(.trigger("falling")) d_ff_11 (
    .clk(and_1_out), .D(D[2]), .Q(Q[2]), .reset(Reset));  // open: Qn, preset, en
  D_Flip_Flop #(.trigger("falling")) d_ff_12 (
    .clk(and_1_out), .D(D[0]), .Q(Q[0]), .reset(Reset));  // open: Qn, preset, en
endmodule

module register_file (
  input  [2:0] rt,
  input  [11:0] in_2,
  input  Write,
  input  [2:0] rs,
  input  [2:0] rd,
  input  Reset,
  output [11:0] rt_2,
  output [11:0] rs_2
);

  wire clock_1_out, demultiplexer_1_out0, demultiplexer_1_out1, demultiplexer_1_out2, demultiplexer_1_out3,
       demultiplexer_1_out4, demultiplexer_1_out5, demultiplexer_1_out6, demultiplexer_1_out7;
  wire [11:0] register_1_q, register_2_q, register_3_q, register_4_q, register_5_q, register_6_q,
       register_7_q, register_8_q;

  Demultiplexer #(.select(3)) demultiplexer_1 (
    .out0(demultiplexer_1_out0), .out1(demultiplexer_1_out1), .out2(demultiplexer_1_out2),
    .out3(demultiplexer_1_out3), .out4(demultiplexer_1_out4), .out5(demultiplexer_1_out5),
    .out6(demultiplexer_1_out6), .out7(demultiplexer_1_out7), .in(Write), .sel(rd));  // open: en
  Clock clock_1 (.out(clock_1_out));
  register register_1 (.D(in_2), .Clock(clock_1_out), .Write(demultiplexer_1_out0), .Reset(Reset), .Q(register_1_q));
  register register_2 (.D(in_2), .Clock(clock_1_out), .Write(demultiplexer_1_out1), .Reset(Reset), .Q(register_2_q));
  register register_3 (.D(in_2), .Clock(clock_1_out), .Write(demultiplexer_1_out2), .Reset(Reset), .Q(register_3_q));
  register register_4 (.D(in_2), .Clock(clock_1_out), .Write(demultiplexer_1_out3), .Reset(Reset), .Q(register_4_q));
  register register_5 (.D(in_2), .Clock(clock_1_out), .Write(demultiplexer_1_out4), .Reset(Reset), .Q(register_5_q));
  register register_6 (.D(in_2), .Clock(clock_1_out), .Write(demultiplexer_1_out5), .Reset(Reset), .Q(register_6_q));
  register register_7 (.D(in_2), .Clock(clock_1_out), .Write(demultiplexer_1_out6), .Reset(Reset), .Q(register_7_q));
  register register_8 (.D(in_2), .Clock(clock_1_out), .Write(demultiplexer_1_out7), .Reset(Reset), .Q(register_8_q));
  Multiplexer #(.select(3), .width(12)) multiplexer_1 (
    .in0(register_1_q), .in1(register_2_q), .in2(register_3_q), .in3(register_4_q), .in4(register_5_q),
    .in5(register_6_q), .in6(register_7_q), .in7(register_8_q), .out(rt_2), .sel(rt));  // open: en
  Multiplexer #(.select(3), .width(12)) multiplexer_2 (
    .in0(register_1_q), .in1(register_2_q), .in2(register_3_q), .in3(register_4_q), .in4(register_5_q),
    .in5(register_6_q), .in6(register_7_q), .in7(register_8_q), .out(rs_2), .sel(rs));  // open: en
endmodule

module counter (
  input  Clock,
  input  [11:0] Reset_match,
  output [11:0] Output
);

  wire comparator_1_eq, comparator_1_gt, or_1_out;
  wire [11:0] n12_bit_carry_lookahead_1_s;

  register register_1 (.D(n12_bit_carry_lookahead_1_s), .Clock(Clock), .Write(1'b1), .Reset(or_1_out), .Q(Output));
  _12_bit_Carry_Lookahead u_12_bit_carry_lookahead_1 (
    .Ci(1'b0), .A(12'h1), .B(Output), .S(n12_bit_carry_lookahead_1_s));  // open: Overflow__Co
  Comparator #(.width(12)) comparator_1 (
    .a(Output), .b(Reset_match), .gt(comparator_1_gt), .eq(comparator_1_eq));  // open: lt
  or or_1 (or_1_out, comparator_1_gt, comparator_1_eq);
endmodule

module finate_state_machine (
);

  wire and_1_out, and_2_out, and_3_out, and_4_out, clock_1_out, comparator_1_eq, comparator_1_gt,
       comparator_1_lt, comparator_2_lt, comparator_3_eq, comparator_3_gt, comparator_3_lt, comparator_4_eq,
       comparator_4_gt, comparator_4_lt, comparator_5_eq, comparator_5_gt, comparator_5_lt, not_1_out,
       not_2_out, or_1_out, or_2_out, or_3_out, or_4_out;
  wire [11:0] counter_1_output;

  Clock clock_1 (.out(clock_1_out));
  counter counter_1 (.Clock(clock_1_out), .Reset_match(12'h1c), .Output(counter_1_output));
  Comparator #(.width(12)) comparator_1 (
    .a(counter_1_output), .b(12'h8), .gt(comparator_1_gt), .eq(comparator_1_eq), .lt(comparator_1_lt));
  Comparator #(.width(12)) comparator_2 (.a(counter_1_output), .b(12'hc), .lt(comparator_2_lt));  // open: gt, eq
  Comparator #(.width(12)) comparator_3 (
    .a(counter_1_output), .b(12'he), .gt(comparator_3_gt), .eq(comparator_3_eq), .lt(comparator_3_lt));
  Comparator #(.width(12)) comparator_4 (
    .a(counter_1_output), .b(12'h16), .gt(comparator_4_gt), .eq(comparator_4_eq), .lt(comparator_4_lt));
  Comparator #(.width(12)) comparator_5 (
    .a(counter_1_output), .b(12'h1a), .gt(comparator_5_gt), .eq(comparator_5_eq), .lt(comparator_5_lt));
  or or_1 (or_1_out, comparator_1_eq, and_1_out);
  and and_1 (and_1_out, comparator_1_gt, comparator_2_lt);
  and and_2 (and_2_out, comparator_4_lt, comparator_3_gt);
  or or_2 (or_2_out, comparator_4_gt, comparator_4_eq);
  not not_1 (not_1_out, comparator_1_lt);
  and and_3 (and_3_out, not_1_out, not_2_out);
  not not_2 (not_2_out, or_1_out);
  or or_3 (or_3_out, and_2_out, comparator_3_eq);
  and and_4 (and_4_out, or_2_out, comparator_5_lt);
  or or_4 (or_4_out, comparator_3_lt, comparator_5_gt, comparator_5_eq);
  LED led_1 (.in(and_3_out));
  LED led_2 (.in(or_1_out));
  LED led_3 (.in(comparator_1_lt));
  LED led_4 (.in(or_4_out));
  LED led_5 (.in(and_4_out));
  LED led_6 (.in(or_3_out));
endmodule

module stack (
  input  Push,
  input  Pop,
  input  Reset,
  input  [11:0] Data,
  output Error,
  output [11:0] Top
);

  wire and_1_out, and_3_out, and_4_out, and_5_out, clock, comparator_1_lt, nor_1_out, not_1_out, not_2_out,
       or_1_out, xor_1_out;
  wire [11:0] adder_1_out, and_2_out, bit_extender_1_out, multiplexer_1_out, multiplexer_2_out, ram_1_data,
       register_1_q, subtractor_1_out;

  Clock u_Clock (.out(clock));
  not not_1 (not_1_out, Pop);
  assign bit_extender_1_out = {{11{not_1_out}}, not_1_out};  // Bit_Extender bit_extender_1
  nor nor_1 (nor_1_out, Pop, Push);
  xor xor_1 (xor_1_out, Pop, Push);
  and and_1 (and_1_out, Pop, Push);
  assign and_2_out = bit_extender_1_out & Data;  // AND_Gate and_2, 12 bits wide
  and and_3 (and_3_out, ~Error, xor_1_out);  // AND_Gate
  register register_1 (.D(multiplexer_2_out), .Clock(clock), .Write(and_3_out), .Reset(Reset), .Q(register_1_q));
  Multiplexer #(.width(12), .enable("false")) multiplexer_1 (
    .in0(register_1_q), .in1(subtractor_1_out), .out(multiplexer_1_out), .sel(or_1_out));
  and and_4 (and_4_out, ~Push, Pop);  // AND_Gate
  Adder #(.width(12)) adder_1 (.a({12{1'b0}}), .b(register_1_q), .out(adder_1_out), .cin(xor_1_out));  // open: cout
  Subtractor #(.width(12)) subtractor_1 (.a(register_1_q), .b(12'h1), .out(subtractor_1_out));  // open: bin, bout
  and and_5 (and_5_out, xor_1_out, not_2_out);
  not not_2 (not_2_out, Error);
  Multiplexer #(.width(12), .enable("false")) multiplexer_2 (
    .in0(adder_1_out), .in1(subtractor_1_out), .out(multiplexer_2_out), .sel(and_4_out));
  or or_1 (or_1_out, and_4_out, nor_1_out);
  Comparator #(.width(12)) comparator_1 (.a(multiplexer_2_out), .b({12{1'b0}}), .lt(comparator_1_lt));  // open: gt, eq
  RAM #(.addrWidth(12), .dataWidth(12), .bus("separate")) ram_1 (
    .addr(multiplexer_1_out), .din(and_2_out), .data(ram_1_data), .str(and_5_out), .clk(clock),
    .ld(nor_1_out), .clr(Reset));  // open: sel
  or or_2 (Error, comparator_1_lt, and_1_out);
  Multiplexer #(.width(12), .enable("false")) multiplexer_3 (
    .in0({12{1'b0}}), .in1(ram_1_data), .out(Top), .sel(nor_1_out));
endmodule
