// Logisim project FD_Group31.circ as structural Verilog: 6 circuits, main circuit main
module main (
  output [11:0] pc,
  output [11:0] r0,
  output [11:0] r1,
  output [11:0] r2,
  output [11:0] r3,
  output [11:0] r4,
  output [11:0] r5,
  output [11:0] r6,
  output [11:0] r7,
  output halt
);

  wire and_2_out, brnz, clock, clock_1_out, comparator_1_eq, controller_circuit_1_imm,
       controller_circuit_1_imm_for_mem, controller_circuit_1_rd, exception, halt_1_halt, j, jal, jr, ldi,
       lui, lw, not_1_out, not_2_out, or_5_out, overflow, reset, sw, write;
  wire [1:0] or_3_out;
  wire [1:1] or_2_out;
  wire [2:0] multiplexer_3_out, op, rd_t, rs_t, rt_t;
  wire [3:0] ALU_op, funct;
  wire [11:0] ALU, data, imm, imm_for_j, imm_signed, immmem, instruction_decoder_1_immediate_unsigned,
       multiplexer_1_out, multiplexer_2_out, multiplexer_5_out, multiplexer_6_out, multiplexer_7_out,
       multiplexer_8_out, multiplexer_10_out, n12_bit_alu_1_result, PC___1, RD, Rs, Rt;
  wire [15:0] ram_1_data;

  Halt halt_1 (.instruction(ram_1_data), .clock(clock_1_out), .reset(reset), .halt(halt_1_halt));
  Clock clock_1 (.out(clock_1_out));
  Button u_reset (.out(reset));
  or or_1 (halt, exception, overflow, halt_1_halt);
  and and_1 (clock, ~halt, clock_1_out);  // AND_Gate
  Multiplexer #(.select(2), .width(12)) multiplexer_1 (
    .in0(imm_signed), .in2(ALU), .in3(imm_for_j), .out(multiplexer_1_out), .sel(or_3_out));  // open: in1, en
  or or_2 (or_2_out[1], jal, lw);
  Comparator #(.width(12)) comparator_1 (.a(RD), .b({12{1'b0}}), .eq(comparator_1_eq));  // open: gt, lt
  not not_1 (not_1_out, comparator_1_eq);
  pc pc_1 (
    .branch_Relative(and_2_out), .branch_Absolute(or_3_out[1]), .Branch_Value(multiplexer_1_out),
    .Clock(clock), .reset(reset), .instruction_address(pc), .PC__1(PC___1));
  Multiplexer #(.select(2), .width(12)) multiplexer_2 (
    .in0(ALU), .in2(data), .in3(PC___1), .out(multiplexer_2_out), .sel({or_2_out[1], jal}));  // open: in1, en
  RAM #(.addrWidth(12), .dataWidth(16)) ram_1 (
    .addr(pc), .data(ram_1_data), .clk(clock), .clr(reset));  // open: sel, ld
  and and_2 (and_2_out, not_1_out, brnz);
  or or_3 (or_3_out[0], j, jal);
  or or_4 (or_3_out[1], or_3_out[0], jr);
  not not_2 (not_2_out, write);
  Multiplexer #(.width(3)) multiplexer_3 (.in0(rd_t), .in1(3'b111), .out(multiplexer_3_out), .sel(jal));  // open: en
  instruction_decoder instruction_decoder_1 (
    .Instruction(ram_1_data), .Operation_code(op), .rd(rd_t), .rs(rs_t), .rt(rt_t), .Function_code(funct),
    .immidiate_for_mem(immmem), .immediate_unsigned(instruction_decoder_1_immediate_unsigned),
    .immediate_signed(imm_signed), .imm_for_j(imm_for_j));
  Multiplexer #(.width(12)) multiplexer_4 (
    .in0(instruction_decoder_1_immediate_unsigned), .in1(imm_signed), .out(imm), .sel(ldi));  // open: en
  register_file register_file_1 (
    .in_2(multiplexer_2_out), .Write(not_2_out), .Reset(reset), .r0(r0), .r1(r1), .r2(r2), .r3(r3), .r4(r4),
    .r5(r5), .r6(r6), .r7(r7), .rt_2(Rt), .rs_2(Rs), .rt(rt_t), .rd(multiplexer_3_out), .rs(rs_t),
    .clock(clock));
  Controller_circuit controller_circuit_1 (
    .Op_code(op), .Func_code(funct), .ALU_op(ALU_op), .RD(controller_circuit_1_rd), .ldi(ldi), .lui(lui),
    .lw(lw), .sw(sw), .imm(controller_circuit_1_imm), .imm_for_mem(controller_circuit_1_imm_for_mem),
    .brnz(brnz), .jr(jr), .write(write), .j(j), .jal(jal));
  exception_controller Exception_controller (.op(op), .rs(rs_t), .rt(rt_t), .funct(funct), .exception(exception));
  Multiplexer #(.width(12)) multiplexer_5 (
    .in0(imm), .in1(immmem), .out(multiplexer_5_out), .sel(controller_circuit_1_imm_for_mem));  // open: en
  Multiplexer #(.width(12), .enable("false")) multiplexer_6 (
    .in0(Rs), .in1(multiplexer_5_out), .out(multiplexer_6_out), .sel(ldi));
  Multiplexer #(.width(12)) multiplexer_7 (
    .in0(Rt), .in1(multiplexer_5_out), .out(multiplexer_7_out), .sel(controller_circuit_1_imm));  // open: en
  Multiplexer #(.width(12)) multiplexer_8 (
    .in0(multiplexer_6_out), .in1(RD), .out(multiplexer_8_out), .sel(controller_circuit_1_rd));  // open: en
  _12_bit_ALU u_12_bit_alu_1 (
    .ALU_code(ALU_op), .a(multiplexer_8_out), .b(multiplexer_7_out), .overflow(overflow),
    .result(n12_bit_alu_1_result));
  Multiplexer #(.width(12)) multiplexer_9 (
    .in0(n12_bit_alu_1_result), .in1({imm[8:0], 3'b000}), .out(ALU), .sel(lui));  // open: en
  Multiplexer #(.width(12)) multiplexer_10 (.in1(ALU), .out(multiplexer_10_out), .sel(or_5_out));  // open: in0, en
  or or_5 (or_5_out, sw, lw);
  RAM #(.addrWidth(12), .dataWidth(12)) ram_2 (
    .addr(multiplexer_10_out), .data(data), .clk(clock), .ld(lw), .clr(reset));  // open: sel
  Multiplexer #(.width(12)) multiplexer_11 (.in1(RD), .out(data), .sel(sw));  // open: in0, en
  Multiplexer #(.select(3), .width(12)) multiplexer_12 (
    .in0(r0), .in1(r1), .in2(r2), .in3(r3), .in4(r4), .in5(r5), .in6(r6), .in7(r7), .out(RD), .sel(rd_t));  // open: en

  // Notes on the sheet:
  //   current instruction
  //   clock signal
  //   reset button
  //   Instructions
  //   DO NOT CHANGE THE INPUTS AND OUTPUTS OF THIS CIRCUIT! Do not add/remove inputs or outputs. Do not even change their location or orientation.
  //   Data
endmodule

module Halt (
  input  [15:0] instruction,
  input  clock,
  input  reset,
  output halt
);

  wire and_1_out, comparator_1_eq, comparator_2_gt, counter_1_carry, or_1_out, or_2_out;
  wire [11:0] counter_1_q;

  Comparator #(.width(16), .mode("unsigned")) comparator_1 (
    .a(instruction), .b({16{1'b0}}), .eq(comparator_1_eq));  // open: gt, lt
  Counter #(.width(12), .max('hfff), .trigger("falling")) counter_1 (
    .Q(counter_1_q), .carry(counter_1_carry), .clk(clock), .clr(reset));  // open: load, D, count
  or or_1 (or_1_out, comparator_1_eq, counter_1_carry);
  Comparator #(.width(12), .mode("unsigned")) comparator_2 (
    .a(counter_1_q), .b({12{1'b0}}), .gt(comparator_2_gt));  // open: eq, lt
  or or_2 (or_2_out, halt, and_1_out);
  and and_1 (and_1_out, or_1_out, comparator_2_gt);
  Register #(.width(1)) register_1 (.D(or_2_out), .Q(halt), .clk(clock), .clr(reset));  // open: en

  // Notes on the sheet:
  //   halt becomes and stays asserted if the instruction is 0000 (not in the first clock cycle) or the end of the counter is reached (2^12)
endmodule

module instruction_decoder (
  input  [15:0] Instruction,
  output [2:0] Operation_code,
  output [2:0] rd,
  output [2:0] rs,
  output [2:0] rt,
  output [3:0] Function_code,
  output [11:0] immidiate_for_mem,
  output [11:0] immediate_unsigned,
  output [11:0] immediate_signed,
  output [11:0] imm_for_j
);

  Multiplexer #(.width(3)) multiplexer_1 (
    .in0(3'b000), .in1(3'b111), .out(immediate_signed[11:9]), .sel(Instruction[9]));  // open: en

  assign Function_code = Instruction[3:0];
  assign imm_for_j = Instruction[12:1];
  assign immediate_signed[8:0] = Instruction[9:1];
  assign immediate_unsigned = {3'b000, Instruction[9:1]};
  assign immidiate_for_mem = {{6{1'b0}}, Instruction[6:1]};
  assign Operation_code = Instruction[15:13];
  assign rd = Instruction[12:10];
  assign rs = Instruction[9:7];
  assign rt = Instruction[6:4];
endmodule

module Controller_circuit (
  input  [2:0] Op_code,
  input  [3:0] Func_code,
  output [3:0] ALU_op,
  output RD,
  output ldi,
  output lui,
  output lw,
  output sw,
  output imm,
  output imm_for_mem,
  output brnz,
  output jr,
  output write,
  output j,
  output jal
);

  wire and_1_out, and_2_out, comparator_1_eq, comparator_2_eq, comparator_3_eq, comparator_4_eq,
       comparator_5_eq, not_1_out, not_2_out, not_3_out, not_4_out;
  wire [3:0] adder_1_out, multiplexer_1_out;

  Adder #(.width(4)) adder_1 (.a(Func_code), .b(4'b1000), .out(adder_1_out));  // open: cin, cout
  Comparator #(.width(3)) comparator_1 (.a(Op_code), .b(3'b100), .eq(comparator_1_eq));  // open: gt, lt
  Comparator #(.width(3)) comparator_2 (.a(Op_code), .b(3'b011), .eq(comparator_2_eq));  // open: gt, lt
  Comparator #(.width(3)) comparator_3 (.a(Op_code), .b(3'b111), .eq(comparator_3_eq));  // open: gt, lt
  Comparator #(.width(3)) comparator_4 (.a(Op_code), .b(3'b101), .eq(comparator_4_eq));  // open: gt, lt
  Comparator #(.width(3)) comparator_5 (.a(Op_code), .b(3'b110), .eq(comparator_5_eq));  // open: gt, lt
  Multiplexer #(.select(3), .width(4)) multiplexer_1 (
    .in0(4'b1110), .in1(Func_code), .in2(adder_1_out), .in3(4'b1111), .in4(4'b0001), .in5(4'b0000),
    .in6(4'b1110), .in7(4'b0000), .out(multiplexer_1_out), .sel(Op_code));  // open: en
  not not_1 (not_1_out, Func_code[0]);
  not not_2 (not_2_out, Func_code[0]);
  not not_3 (not_3_out, Func_code[0]);
  not not_4 (not_4_out, Func_code[0]);
  and and_1 (and_1_out, comparator_1_eq, not_1_out);
  and and_2 (and_2_out, comparator_1_eq, Func_code[0]);
  and and_3 (ldi, comparator_2_eq, not_2_out);
  and and_4 (lui, comparator_2_eq, Func_code[0]);
  and and_5 (lw, comparator_3_eq, not_3_out);
  and and_6 (sw, comparator_3_eq, Func_code[0]);
  and and_7 (jr, comparator_4_eq, Func_code[0]);
  and and_8 (brnz, comparator_4_eq, not_4_out);
  and and_9 (jal, comparator_5_eq, Func_code[0]);
  and and_10 (j, comparator_5_eq, ~Func_code[0]);  // AND_Gate
  Multiplexer #(.width(4)) multiplexer_2 (
    .in0(multiplexer_1_out), .in1(4'b0000), .out(ALU_op), .sel(and_1_out));  // open: en
  or or_1 (RD, and_1_out, jr, and_2_out);
  or or_2 (imm, lw, and_1_out, and_2_out, jr, ldi, lui, sw);
  or or_3 (imm_for_mem, lw, sw);
  or or_4 (write, jr, brnz, sw, j);
endmodule

module pc (
  input  branch_Relative,
  input  branch_Absolute,
  input  [11:0] Branch_Value,
  input  Clock,
  input  reset,
  output [11:0] instruction_address,
  output [11:0] PC__1
);

  wire [1:1] or_1_out;
  wire [11:0] multiplexer_1_out, n12_bit_carry_lookahead_2_s;

  register register_1 (.D(multiplexer_1_out), .Clock(Clock), .Write(1'b1), .Reset(reset), .Q(instruction_address));
  or or_1 (or_1_out[1], branch_Relative, branch_Absolute);
  _12_bit_Carry_Lookahead u_12_bit_carry_lookahead_1 (
    .Ci(1'b0), .A(instruction_address), .B(12'h1), .S(PC__1));  // open: Overflow__Co
  _12_bit_Carry_Lookahead u_12_bit_carry_lookahead_2 (
    .Ci(1'b1), .A(instruction_address), .B(Branch_Value), .S(n12_bit_carry_lookahead_2_s));  // open: Overflow__Co
  Multiplexer #(.select(2), .width(12)) multiplexer_1 (
    .in0(PC__1), .in2(n12_bit_carry_lookahead_2_s), .in3(Branch_Value), .out(multiplexer_1_out),
    .sel({or_1_out[1], branch_Absolute}));  // open: in1, en
endmodule

module exception_controller (
  input  [2:0] op,
  input  [2:0] rs,
  input  [2:0] rt,
  input  [3:0] funct,
  output exception
);

  wire comparator_1_eq, comparator_2_eq, not_1_out, not_2_out;
  wire [9:0] demultiplexer_1_out0, demultiplexer_1_out1, demultiplexer_1_out2;

  Demultiplexer #(.select(3), .width(10)) demultiplexer_1 (
    .out0(demultiplexer_1_out0), .out1(demultiplexer_1_out1), .out2(demultiplexer_1_out2),
    .in({rs, rt, funct}), .sel(op));  // open: out3, out4, out5, out6, out7, en
  Comparator #(.width(10), .mode("unsigned")) comparator_1 (
    .a(demultiplexer_1_out0), .b({10{1'b0}}), .eq(comparator_1_eq));  // open: gt, lt
  not not_1 (not_1_out, comparator_1_eq);
  not not_2 (not_2_out, comparator_2_eq);
  Comparator #(.width(4), .mode("unsigned")) comparator_2 (
    .a(demultiplexer_1_out2[6:3]), .b(4'b0000), .eq(comparator_2_eq));  // open: gt, lt
  or or_1 (exception, not_1_out, demultiplexer_1_out1[3], not_2_out);
endmodule
