// Logisim project Register.circ as structural Verilog: 2 circuits, main circuit register
module register (
  input  [11:0] D,
  input  Clock,
  input  Write,
  input  Reset,
  output [11:0] Q
);

  wire and_1_out;

  Clock clock_1 ();  // open: out
  and and_1 (and_1_out, Clock, Write);
  D_Flip_Flop #(.trigger("falling")) d_ff_1 (
    .clk(and_1_out), .D(D[11]), .Q(Q[11]), .reset(Reset));  // open: Qn, preset, en
  D_Flip_Flop #(.trigger("falling")) d_ff_2 (
    .clk(and_1_out), .D(D[9]), .Q(Q[9]), .reset(Reset));  // open: Qn, preset, en
  D_Flip_Flop #(.trigger("falling")) d_ff_3 (
    .clk(and_1_out), .D(D[10]), .Q(Q[10]), .reset(Reset));  // open: Qn, preset, en
  D_Flip_Flop #(.trigger("falling")) d_ff_4 (
    .clk(and_1_out), .D(D[7]), .Q(Q[7]), .reset(Reset));  // open: Qn, preset, en
  D_Flip_Flop #(.trigger("falling")) d_ff_5 (
    .clk(and_1_out), .D(D[8]), .Q(Q[8]), .reset(Reset));  // open: Qn, preset, en
  D_Flip_Flop #(.trigger("falling")) d_ff_6 (
    .clk(and_1_out), .D(D[5]), .Q(Q[5]), .reset(Reset));  // open: Qn, preset, en
  D_Flip_Flop #(.trigger("falling")) d_ff_7 (
    .clk(and_1_out), .D(D[6]), .Q(Q[6]), .reset(Reset));  // open: Qn, preset, en
  D_Flip_Flop #(.trigger("falling")) d_ff_8 (
    .clk(and_1_out), .D(D[3]), .Q(Q[3]), .reset(Reset));  // open: Qn, preset, en
  D_Flip_Flop #(.trigger("falling")) d_ff_9 (
    .clk(and_1_out), .D(D[4]), .Q(Q[4]), .reset(Reset));  // open: Qn, preset, en
  D_Flip_Flop #(.trigger("falling")) d_ff_10 (
    .clk(and_1_out), .D(D[1]), .Q(Q[1]), .reset(Reset));  // open: Qn, preset, en
  D_Flip_Flop #(.trigger("falling")) d_ff_11 (
    .clk(and_1_out), .D(D[2]), .Q(Q[2]), .reset(Reset));  // open: Qn, preset, en
  D_Flip_Flop #(.trigger("falling")) d_ff_12 (
    .clk(and_1_out), .D(D[0]), .Q(Q[0]), .reset(Reset));  // open: Qn, preset, en
endmodule

module register_file (
  input  [2:0] rt,
  input  [11:0] in_2,
  input  Write,
  input  [2:0] rs,
  input  [2:0] rd,
  input  clock,
  input  Reset,
  output [11:0] r0,
  output [11:0] r1,
  output [11:0] r2,
  output [11:0] r3,
  output [11:0] r4,
  output [11:0] r5,
  output [11:0] r6,
  output [11:0] r7,
  output [11:0] rt_2,
  output [11:0] rs_2
);

  wire demultiplexer_1_out0, demultiplexer_1_out1, demultiplexer_1_out2, demultiplexer_1_out3,
       demultiplexer_1_out4, demultiplexer_1_out5, demultiplexer_1_out6, demultiplexer_1_out7;

  Demultiplexer #(.select(3)) demultiplexer_1 (
    .out0(demultiplexer_1_out0), .out1(demultiplexer_1_out1), .out2(demultiplexer_1_out2),
    .out3(demultiplexer_1_out3), .out4(demultiplexer_1_out4), .out5(demultiplexer_1_out5),
    .out6(demultiplexer_1_out6), .out7(demultiplexer_1_out7), .in(Write), .sel(rd));  // open: en
  register register_1 (.D(in_2), .Clock(clock), .Write(demultiplexer_1_out0), .Reset(Reset), .Q(r0));
  register register_2 (.D(in_2), .Clock(clock), .Write(demultiplexer_1_out1), .Reset(Reset), .Q(r1));
  register register_3 (.D(in_2), .Clock(clock), .Write(demultiplexer_1_out2), .Reset(Reset), .Q(r2));
  register register_4 (.D(in_2), .Clock(clock), .Write(demultiplexer_1_out3), .Reset(Reset), .Q(r3));
  register register_5 (.D(in_2), .Clock(clock), .Write(demultiplexer_1_out4), .Reset(Reset), .Q(r4));
  register register_6 (.D(in_2), .Clock(clock), .Write(demultiplexer_1_out5), .Reset(Reset), .Q(r5));
  register register_7 (.D(in_2), .Clock(clock), .Write(demultiplexer_1_out6), .Reset(Reset), .Q(r6));
  register register_8 (.D(in_2), .Clock(clock), .Write(demultiplexer_1_out7), .Reset(Reset), .Q(r7));
  Multiplexer #(.select(3), .width(12)) multiplexer_1 (
    .in0(r0), .in1(r1), .in2(r2), .in3(r3), .in4(r4), .in5(r5), .in6(r6), .in7(r7), .out(rt_2), .sel(rt));  // open: en
  Multiplexer #(.select(3), .width(12)) multiplexer_2 (
    .in0(r0), .in1(r1), .in2(r2), .in3(r3), .in4(r4), .in5(r5), .in6(r6), .in7(r7), .out(rs_2), .sel(rs));  // open: en
endmodule
